# Fritzing sketch Node (saved by Fritzing 0.8.7b)
circuit board: 4.19253cm x 4.31979cm
breadboards: 1

parts:
  Ethernet = double row male pin header, 10 pins [form="♂ (male)"]
  RFID = male pin header, 8 pins [form="♂ (male)"]
  Relay_out = male pin header, 3 pins [form="♂ (male)"]
  LEDs_out = male pin header, 4 pins [form="♂ (male)"]
  R1 = Resistor [tolerance=±5% resistance=220 package=THT]
  R2 = Resistor [tolerance=±5% resistance=220 package=THT]
  R3 = Resistor [tolerance=±5% resistance=220 package=THT]
  Atmega1 = atmega328 [package=dip]
  XTAL1 = Crystal [frequency="16 Mhz" package=THT]
  C1_20pF = Capacitor [package=cap-pth-small2]
  C2_20pF1 = Capacitor [package=cap-pth-small2]
  J1 = Power Jack [package=power_jack_pth_lock]

nets:
  INT: Ethernet.pin1
  MISO: Ethernet.pin2, RFID.pin4, Atmega1.D11_(PWM)
  SCK: Ethernet.pin3, RFID.pin2, Atmega1.D13
  reset: Ethernet.pin4
  GND: Ethernet.pin5, RFID.pin6, Relay_out.pin3, LEDs_out.pin4, Atmega1.GND, C1_20pF.2, C2_20pF1.2, J1.GND, J1.GNDBREAK
  VCC: Ethernet.pin6, RFID.pin8, Relay_out.pin1, Atmega1.RESET, Atmega1.VCC, Atmega1.AVCC, J1.PWR
  CS-ETHER: Ethernet.pin7, Atmega1.D8
  MOSI: Ethernet.pin8, RFID.pin3, Atmega1.D12
  WOL: Ethernet.pin9
  CLKOUT: Ethernet.pin10
  CS-rfid: RFID.pin1, Atmega1.D9_(PWM)
  IRQ: RFID.pin5
  RST: RFID.pin7
  relay: Relay_out.pin2, Atmega1.D7
  N1: LEDs_out.pin1, R1.Pin_1
  N2: LEDs_out.pin2, R2.Pin_1
  N3: LEDs_out.pin3, R3.Pin_1
  Red: R1.Pin_0, Atmega1.D2
  Orange: R2.Pin_0, Atmega1.D3_(PWM)
  Green: R3.Pin_0, Atmega1.D4
  N4: Atmega1.XLAT1, XTAL1.pin_0, C1_20pF.1
  N5: Atmega1.XLAT2, XTAL1.pin_1, C2_20pF1.1
